// Digital circuit Circuito_Principal_RISC-V.dig as structural Verilog
module Circuito_Principal_RISC_V (
  input  CLK,
  input  Reset,
  input  clk_2,
  output [31:0] PC___saida,
  output [31:0] IM___saida,
  output [31:0] MUX_MEM_WB,
  output Reg_Write,
  output [31:0] Saida_RAM__memoria_dados,
  output [31:0] Resultado_ALU
);

  wire and_2_out, comparator_1_eq, not_1_out, or_1_out, switchdt_1_p3, u_alu_zero, u_control_alu_src,
       u_control_branch, u_control_is_vector, u_control_mem_read, u_control_mem_to_reg, u_control_mem_write,
       u_control_reg_write, u_ex_mem_reg_mem_read_out, u_ex_mem_reg_mem_to_reg_out,
       u_ex_mem_reg_mem_write_out, u_ex_mem_reg_reg_write_out, u_hazard_unit_stall, u_id_ex_reg_alu_src_out,
       u_id_ex_reg_branch_out, u_id_ex_reg_is_vector_out, u_id_ex_reg_mem_read_out,
       u_id_ex_reg_mem_to_reg_out, u_id_ex_reg_mem_write_out, u_id_ex_reg_reg_write_out,
       u_mem_wb_reg_mem_to_reg_out, u_pipeline_ctrl_id_ex_flush, u_pipeline_ctrl_if_id_flush,
       u_pipeline_ctrl_if_id_write, u_pipeline_ctrl_pc_write, xor_1_out;
  wire [1:0] comparator_2_eq, u_control_alu_op, u_forwarding_unit_forwarda, u_forwarding_unit_forwardb,
       u_id_ex_reg_alu_op_out;
  wire [2:0] u_id_ex_reg_funct3_out;
  wire [4:0] u_ex_mem_reg_rd_out, u_id_ex_reg_rd_out, u_id_ex_reg_rs1_out, u_id_ex_reg_rs2_out,
       u_mem_wb_reg_rd_out;
  wire [5:0] u_alu_control_alu_ctrl;
  wire [6:0] u_id_ex_reg_funct7_out;
  wire [31:0] and_1_out, Branch_JAL_s, JARL_s, multiplexer_1_out, multiplexer_2_out, multiplexer_3_out,
       multiplexer_4_out, Somador_PC_plus_4_s, u_ex_mem_reg_alu_result_out, u_ex_mem_reg_write_data_out,
       u_id_ex_reg_imm_out, u_id_ex_reg_pc_out, u_id_ex_reg_read_data1_out, u_id_ex_reg_read_data2_out,
       u_if_id_reg_instr_out, u_if_id_reg_pc_out, u_imm_gen_imm, u_mem_wb_reg_alu_result_out,
       u_mem_wb_reg_mem_data_out, u_regfile_rd1, u_regfile_rd2;

  // SwitchDT switchdt_1: pin names not known; wires that end beside it: CLK, clk_2, switchdt_1_p3
  Multiplexer #(.Bits(32), .Selector_Bits(2)) multiplexer_1 (
    .sel(comparator_2_eq), .in_0(Somador_PC_plus_4_s), .in_1(Branch_JAL_s), .in_2(and_1_out),
    .in_3({32{1'b0}}), .out(multiplexer_1_out));
  pc #(.applicationType("IVERILOG")) u_pc (
    .clk(switchdt_1_p3), .reset(Reset), .pc_write(u_pipeline_ctrl_pc_write), .next_pc(multiplexer_1_out),
    .pc(PC___saida));
  Add #(.Bits(32)) Somador_PC_plus_4 (.a(32'h4), .b(PC___saida), .c_i(1'b0), .s(Somador_PC_plus_4_s));  // open: c_o
  ROM #(.AddrBits(10), .Bits(32)) Instruction_Memory (.A(PC___saida[11:2]), .sel(1'b1), .D(IM___saida));
  Add #(.Bits(32)) Branch_JAL (.a(u_imm_gen_imm), .b(u_id_ex_reg_pc_out), .c_i(1'b0), .s(Branch_JAL_s));  // open: c_o
  if_id_reg #(.applicationType("IVERILOG")) u_if_id_reg (
    .clk(switchdt_1_p3), .reset(Reset), .if_id_write(u_pipeline_ctrl_if_id_write),
    .flush(u_pipeline_ctrl_if_id_flush), .instr_in(IM___saida), .pc_in(PC___saida),
    .pc_out(u_if_id_reg_pc_out), .instr_out(u_if_id_reg_instr_out));
  control #(.applicationType("IVERILOG")) u_control (
    .opcode(u_if_id_reg_instr_out[6:0]), .reg_write(u_control_reg_write), .mem_to_reg(u_control_mem_to_reg),
    .mem_read(u_control_mem_read), .mem_write(u_control_mem_write), .alu_src(u_control_alu_src),
    .alu_op(u_control_alu_op), .branch(u_control_branch), .is_vector(u_control_is_vector));
  assign and_1_out = 32'hfffffffe & JARL_s;  // And and_1, 32 bits wide
  regfile #(.applicationType("IVERILOG")) u_regfile (
    .clk(switchdt_1_p3), .reset(Reset), .we(Reg_Write), .rs1(u_if_id_reg_instr_out[19:15]),
    .rs2(u_if_id_reg_instr_out[24:20]), .wd(MUX_MEM_WB), .rd(u_mem_wb_reg_rd_out), .rd1(u_regfile_rd1),
    .rd2(u_regfile_rd2));
  imm_gen #(.applicationType("IVERILOG")) u_imm_gen (.instr(u_if_id_reg_instr_out), .imm(u_imm_gen_imm));
  id_ex_reg #(.applicationType("IVERILOG")) u_id_ex_reg (
    .clk(switchdt_1_p3), .reset(Reset), .flush(u_pipeline_ctrl_id_ex_flush),
    .reg_write_in(u_control_reg_write), .mem_to_reg_in(u_control_mem_to_reg),
    .mem_read_in(u_control_mem_read), .mem_write_in(u_control_mem_write), .alu_src_in(u_control_alu_src),
    .alu_op_in(u_control_alu_op), .branch_in(u_control_branch), .is_vector_in(u_control_is_vector),
    .pc_in(u_if_id_reg_pc_out), .read_data1_in(u_regfile_rd1), .read_data2_in(u_regfile_rd2),
    .imm_in(u_imm_gen_imm), .rs1_in(u_if_id_reg_instr_out[19:15]), .rs2_in(u_if_id_reg_instr_out[19:15]),
    .rd_in(u_if_id_reg_instr_out[11:7]), .funct3_in(u_if_id_reg_instr_out[14:12]),
    .funct7_in(u_if_id_reg_instr_out[31:25]), .reg_write_out(u_id_ex_reg_reg_write_out),
    .mem_to_reg_out(u_id_ex_reg_mem_to_reg_out), .mem_read_out(u_id_ex_reg_mem_read_out),
    .mem_write_out(u_id_ex_reg_mem_write_out), .alu_src_out(u_id_ex_reg_alu_src_out),
    .alu_op_out(u_id_ex_reg_alu_op_out), .branch_out(u_id_ex_reg_branch_out),
    .is_vector_out(u_id_ex_reg_is_vector_out), .pc_out(u_id_ex_reg_pc_out),
    .read_data1_out(u_id_ex_reg_read_data1_out), .read_data2_out(u_id_ex_reg_read_data2_out),
    .imm_out(u_id_ex_reg_imm_out), .rs1_out(u_id_ex_reg_rs1_out), .rs2_out(u_id_ex_reg_rs2_out),
    .rd_out(u_id_ex_reg_rd_out), .funct3_out(u_id_ex_reg_funct3_out), .funct7_out(u_id_ex_reg_funct7_out));
  Add #(.Bits(32)) JARL (.a(u_id_ex_reg_read_data1_out), .b(u_id_ex_reg_imm_out), .c_i(1'b0), .s(JARL_s));  // open: c_o
  alu_control #(.applicationType("IVERILOG")) u_alu_control (
    .alu_op(u_id_ex_reg_alu_op_out), .funct3(u_id_ex_reg_funct3_out), .funct7(u_id_ex_reg_funct7_out),
    .is_vector(u_id_ex_reg_is_vector_out), .alu_ctrl(u_alu_control_alu_ctrl));
  Multiplexer #(.Bits(32)) multiplexer_2 (
    .sel(u_id_ex_reg_alu_src_out), .in_0(multiplexer_4_out), .in_1(u_id_ex_reg_imm_out),
    .out(multiplexer_2_out));
  forwarding_unit #(.applicationType("IVERILOG")) u_forwarding_unit (
    .ex_rs1(u_id_ex_reg_rs1_out), .ex_rs2(u_id_ex_reg_rs2_out), .mem_reg_write(u_ex_mem_reg_reg_write_out),
    .mem_rd(u_ex_mem_reg_rd_out), .wb_reg_write(Reg_Write), .wb_rd(u_mem_wb_reg_rd_out),
    .forwardA(u_forwarding_unit_forwarda), .forwardB(u_forwarding_unit_forwardb));
  Multiplexer #(.Selector_Bits(2), .Bits(32)) multiplexer_3 (
    .sel(u_forwarding_unit_forwarda), .in_0(u_id_ex_reg_read_data1_out), .in_1(MUX_MEM_WB),
    .in_2(u_ex_mem_reg_alu_result_out), .in_3({32{1'b0}}), .out(multiplexer_3_out));
  alu #(.applicationType("IVERILOG")) u_alu (
    .a(multiplexer_3_out), .b(multiplexer_2_out), .alu_ctrl(u_alu_control_alu_ctrl), .result(Resultado_ALU),
    .zero(u_alu_zero));
  Multiplexer #(.Bits(32), .Selector_Bits(2)) multiplexer_4 (
    .sel(u_forwarding_unit_forwardb), .in_0(u_id_ex_reg_read_data2_out), .in_1(MUX_MEM_WB),
    .in_2(u_ex_mem_reg_alu_result_out), .in_3({32{1'b0}}), .out(multiplexer_4_out));
  ex_mem_reg #(.applicationType("IVERILOG")) u_ex_mem_reg (
    .clk(switchdt_1_p3), .reset(Reset), .reg_write_in(u_id_ex_reg_reg_write_out),
    .mem_to_reg_in(u_id_ex_reg_mem_to_reg_out), .mem_read_in(u_id_ex_reg_mem_read_out),
    .mem_write_in(u_id_ex_reg_mem_write_out), .branch_in(u_id_ex_reg_branch_out),
    .alu_result_in(Resultado_ALU), .write_data_in(multiplexer_4_out), .rd_in(u_id_ex_reg_rd_out),
    .rs1_in(u_id_ex_reg_rs1_out), .rs2_in(u_id_ex_reg_rs2_out), .reg_write_out(u_ex_mem_reg_reg_write_out),
    .mem_to_reg_out(u_ex_mem_reg_mem_to_reg_out), .mem_read_out(u_ex_mem_reg_mem_read_out),
    .mem_write_out(u_ex_mem_reg_mem_write_out), .alu_result_out(u_ex_mem_reg_alu_result_out),
    .write_data_out(u_ex_mem_reg_write_data_out), .rd_out(u_ex_mem_reg_rd_out));  // open: branch_out, rs1_out, rs2_out
  hazard_unit #(.applicationType("IVERILOG")) u_hazard_unit (
    .id_rs1(u_if_id_reg_instr_out[19:15]), .id_rs2(u_if_id_reg_instr_out[24:20]),
    .ex_mem_read(u_ex_mem_reg_mem_read_out), .ex_rd(u_id_ex_reg_rd_out), .stall(u_hazard_unit_stall));
  RAMAsync #(.AddrBits(10), .Bits(32)) Memoria_de_Dados (
    .A({u_ex_mem_reg_alu_result_out[9:2], 2'b00}), .D(u_ex_mem_reg_write_data_out),
    .we(u_ex_mem_reg_mem_write_out), .Q(Saida_RAM__memoria_dados));
  xor xor_1 (xor_1_out, u_id_ex_reg_funct3_out[0], u_alu_zero);
  Comparator #(.Bits(7)) comparator_1 (
    .a(u_if_id_reg_instr_out[6:0]), .b(7'b1101111), .eq(comparator_1_eq));  // open: gt, lt
  Comparator #(.Bits(7)) comparator_2 (
    .a(u_if_id_reg_instr_out[6:0]), .b(7'b1001111), .eq(comparator_2_eq[1]));  // open: gt, lt
  and and_2 (and_2_out, xor_1_out, u_id_ex_reg_branch_out);
  mem_wb_reg #(.applicationType("IVERILOG")) u_mem_wb_reg (
    .clk(switchdt_1_p3), .reset(Reset), .reg_write_in(u_ex_mem_reg_reg_write_out),
    .mem_to_reg_in(u_ex_mem_reg_mem_to_reg_out), .alu_result_in(u_ex_mem_reg_alu_result_out),
    .mem_data_in(Saida_RAM__memoria_dados), .rd_in(u_ex_mem_reg_rd_out), .reg_write_out(Reg_Write),
    .mem_to_reg_out(u_mem_wb_reg_mem_to_reg_out), .alu_result_out(u_mem_wb_reg_alu_result_out),
    .mem_data_out(u_mem_wb_reg_mem_data_out), .rd_out(u_mem_wb_reg_rd_out));
  or or_1 (or_1_out, comparator_1_eq, and_2_out);
  not not_1 (not_1_out, comparator_2_eq[1]);
  pipeline_ctrl #(.applicationType("IVERILOG")) u_pipeline_ctrl (
    .stall(u_hazard_unit_stall), .branch_taken(and_2_out), .jal_taken(comparator_1_eq),
    .jalr_taken(comparator_2_eq[1]), .pc_write(u_pipeline_ctrl_pc_write),
    .if_id_write(u_pipeline_ctrl_if_id_write), .if_id_flush(u_pipeline_ctrl_if_id_flush),
    .id_ex_flush(u_pipeline_ctrl_id_ex_flush));
  and and_3 (comparator_2_eq[0], or_1_out, not_1_out);
  Multiplexer #(.Bits(32)) multiplexer_5 (
    .sel(u_mem_wb_reg_mem_to_reg_out), .in_0(u_mem_wb_reg_alu_result_out), .in_1(u_mem_wb_reg_mem_data_out),
    .out(MUX_MEM_WB));

  // Notes on the sheet:
  //   Reg_Write: Se deve escrever no registrador no ciclo dado
  //   contents of Instruction_Memory (hex, n*v repeats v):
  //   a00093,1400113,10000193,20000213,11a023,1a283,5102b3,61a223,508463
  //   ,100393,13,13,6600393,2210c63,200413,13,5800413,18004ef,300513
  //   ,13,4d00513,48067,4200593,12345637,d82047,e83047,f12047,1104047
  //   ,120f0b3,120e133,12099b3,115d33,500a93,fffa0a93,fe0a9ae3,13,838b33
  //   ,161a423,81ab83,ab8c33,4*13
  //   IF/ID
  //   BANCO DE REGISTRADORES
  //   ID/EX
  //   MUX ALU SCR
  //   MUX FOWARDING A
  //   MUX FOWARDING B
  //   EX/MEM
  //   branch_taken = (ID/EX.branch_out) && (ALU.zero ^ ID/EX.funct3_out[0])
  //   MEM/WB
endmodule

/* Code of pc:
module pc(
    input clk,
    input reset,           // reset assincrono
    input pc_write,        // enable para stalls
    input [31:0] next_pc,
    output reg [31:0] pc
);
    always @(posedge clk or posedge reset) begin
        if (reset) pc <= 0;
        else if (pc_write) pc <= next_pc;
    end
endmodule
*/

/* Code of if_id_reg:
module if_id_reg(
    input clk, input reset, input if_id_write, input flush,
    input [31:0] instr_in, input [31:0] pc_in,
    output reg [31:0] pc_out, output reg [31:0] instr_out
);
    always @(posedge clk or posedge reset) begin
        if (reset) begin pc_out <= 0; instr_out <= 0; end
        else if (flush) begin pc_out <= 0; instr_out <= 32'h00000013; end
        else if (if_id_write) begin pc_out <= pc_in; instr_out <= instr_in; end
    end
endmodule
*/

/* Code of control:
module control(
    input [6:0] opcode,
    output reg reg_write,
    output reg mem_to_reg,
    output reg mem_read,
    output reg mem_write,
    output reg alu_src,
    output reg [1:0] alu_op,
    output reg branch,
    output reg is_vector
);
    always @(*) begin
        reg_write = 0; mem_to_reg = 0; mem_read = 0;
        mem_write = 0; alu_src = 0; alu_op = 0; 
        branch = 0; is_vector = 0;
        
        case (opcode)
            7'b0110011: begin reg_write = 1; alu_op = 2'b10; end // R-type
            7'b0010011: begin reg_write = 1; alu_src = 1; alu_op = 2'b10; end // I-type
            7'b0000011: begin reg_write = 1; mem_read = 1; mem_to_reg = 1; alu_src = 1; end // LW
            7'b0100011: begin mem_write = 1; alu_src = 1; end // SW
            7'b1100011: begin branch = 1; alu_op = 2'b01; end // Branch
            7'b0110111: begin reg_write = 1; alu_src = 1; alu_op = 2'b11; end // LUI
            7'b0100111: begin reg_write = 1; is_vector = 1; alu_op = 2'b11; end // Vetorial
            default: ; // NOP
        endcase
    end
endmodule
*/

/* Code of regfile:
module regfile(
    input clk,
    input reset,
    input we,
    input [4:0] rs1,
    input [4:0] rs2,
    input [31:0] wd,
    input [4:0] rd,
    output [31:0] rd1,
    output [31:0] rd2
);
    reg [31:0] regs [0:31];
    integer i;
    always @(posedge clk or posedge reset) begin
        if (reset) for (i=0; i<32; i=i+1) regs[i] <= 0;
        else if (we && rd != 0) regs[rd] <= wd;
    end
    assign rd1 = (rs1 != 0) ? regs[rs1] : 0;
    assign rd2 = (rs2 != 0) ? regs[rs2] : 0;
endmodule
*/

/* Code of imm_gen:
module imm_gen(
    input [31:0] instr,    // Instrução completa
    output reg [31:0] imm  // Imediato estendido
);

    always @(*) begin
        case (instr[6:0])  // Baseado no opcode
            // I-type (addi, lw, jalr)
            7'b0010011, 7'b0000011, 7'b1100111: 
                imm = {{20{instr[31]}}, instr[31:20]};
            
            // S-type (sw)
            7'b0100011: 
                imm = {{20{instr[31]}}, instr[31:25], instr[11:7]};
            
            // B-type (beq, bne)
            7'b1100011: 
                imm = {{19{instr[31]}}, instr[31], instr[7], 
                       instr[30:25], instr[11:8], 1'b0};
            
            // U-type (lui)
            7'b0110111: 
                imm = {instr[31:12], 12'b0};
            
            // J-type (jal)
            7'b1101111: 
                imm = {{11{instr[31]}}, instr[31], instr[19:12], 
                       instr[20], instr[30:21], 1'b0};
            
            default: 
                imm = 32'b0;
        endcase
    end

endmodule
*/

/* Code of id_ex_reg:
module id_ex_reg(
    input clk, input reset, input flush,
    input reg_write_in, input mem_to_reg_in, input mem_read_in,
    input mem_write_in, input alu_src_in, input [1:0] alu_op_in,
    input branch_in, input is_vector_in,  // novo
    input [31:0] pc_in, input [31:0] read_data1_in, input [31:0] read_data2_in,
    input [31:0] imm_in, input [4:0] rs1_in, input [4:0] rs2_in,
    input [4:0] rd_in, input [2:0] funct3_in, input [6:0] funct7_in,
    output reg reg_write_out, output reg mem_to_reg_out, output reg mem_read_out,
    output reg mem_write_out, output reg alu_src_out, output reg [1:0] alu_op_out,
    output reg branch_out, output reg is_vector_out,  // novo
    output reg [31:0] pc_out, output reg [31:0] read_data1_out,
    output reg [31:0] read_data2_out, output reg [31:0] imm_out,
    output reg [4:0] rs1_out, output reg [4:0] rs2_out, output reg [4:0] rd_out,
    output reg [2:0] funct3_out, output reg [6:0] funct7_out
);
    always @(posedge clk or posedge reset) begin
        if (reset) begin
            reg_write_out <= 0; mem_to_reg_out <= 0; mem_read_out <= 0;
            mem_write_out <= 0; alu_src_out <= 0; alu_op_out <= 0;
            branch_out <= 0; is_vector_out <= 0;
            pc_out <= 0; read_data1_out <= 0; read_data2_out <= 0;
            imm_out <= 0; rs1_out <= 0; rs2_out <= 0; rd_out <= 0;
            funct3_out <= 0; funct7_out <= 0;
        end else if (flush) begin
            reg_write_out <= 0; mem_to_reg_out <= 0; mem_read_out <= 0;
            mem_write_out <= 0; alu_src_out <= 0; alu_op_out <= 0;
            branch_out <= 0; is_vector_out <= 0;
            pc_out <= pc_in; read_data1_out <= 0; read_data2_out <= 0;
            imm_out <= 0; rs1_out <= 0; rs2_out <= 0; rd_out <= 0;
            funct3_out <= 0; funct7_out <= 0;
        end else begin
            reg_write_out <= reg_write_in; mem_to_reg_out <= mem_to_reg_in;
            mem_read_out <= mem_read_in; mem_write_out <= mem_write_in;
            alu_src_out <= alu_src_in; alu_op_out <= alu_op_in;
            branch_out <= branch_in; is_vector_out <= is_vector_in;
            pc_out <= pc_in; read_data1_out <= read_data1_in;
            read_data2_out <= read_data2_in; imm_out <= imm_in;
            rs1_out <= rs1_in; rs2_out <= rs2_in; rd_out <= rd_in;
            funct3_out <= funct3_in; funct7_out <= funct7_in;
        end
    end
endmodule
*/

/* Code of alu_control:
module alu_control(
    input [1:0] alu_op,
    input [2:0] funct3,
    input [6:0] funct7,
    input is_vector,
    output reg [5:0] alu_ctrl  // 6 bits agora
);
    always @(*) begin
        if (is_vector) begin
            // Modo vetorial: [5:4]=modo, [3:0]=operação
            case (funct3)
                3'b000: alu_ctrl = 6'b01_0000; // vadd.8
                3'b001: alu_ctrl = 6'b10_0000; // vadd.16
                3'b010: alu_ctrl = 6'b01_0001; // vsub.8
                3'b011: alu_ctrl = 6'b10_0001; // vsub.16
                3'b100: alu_ctrl = 6'b01_0010; // vand.8
                3'b101: alu_ctrl = 6'b10_0010; // vand.16
                3'b110: alu_ctrl = 6'b01_0011; // vor.8
                3'b111: alu_ctrl = 6'b10_0011; // vor.16
                default: alu_ctrl = 6'b00_0000;
            endcase
        end else begin
            // Modo escalar
            alu_ctrl[5:4] = 2'b00; // modo escalar
            case (alu_op)
                2'b00: alu_ctrl[3:0] = 4'b0000; // ADD
                2'b01: alu_ctrl[3:0] = 4'b0001; // SUB
                2'b10: begin
                    case (funct3)
                        3'b000: alu_ctrl[3:0] = (funct7[5]) ? 4'b0001 : 4'b0000;
                        3'b001: alu_ctrl[3:0] = 4'b0101;
                        3'b010: alu_ctrl[3:0] = 4'b0001;
                        3'b011: alu_ctrl[3:0] = 4'b0001;
                        3'b100: alu_ctrl[3:0] = 4'b0100;
                        3'b101: alu_ctrl[3:0] = (funct7[5]) ? 4'b0111 : 4'b0110;
                        3'b110: alu_ctrl[3:0] = 4'b0011;
                        3'b111: alu_ctrl[3:0] = 4'b0010;
                        default: alu_ctrl[3:0] = 4'b0000;
                    endcase
                end
                2'b11: alu_ctrl[3:0] = 4'b1000; // LUI
                default: alu_ctrl[3:0] = 4'b0000;
            endcase
        end
    end
endmodule
*/

/* Code of forwarding_unit:
module forwarding_unit(
    input [4:0] ex_rs1,
    input [4:0] ex_rs2,
    input mem_reg_write,
    input [4:0] mem_rd,
    input wb_reg_write,
    input [4:0] wb_rd,
    output reg [1:0] forwardA,
    output reg [1:0] forwardB
);
    always @(*) begin
        forwardA = 2'b00;
        forwardB = 2'b00;
        
        // Forward A
        if (mem_reg_write && mem_rd != 0 && mem_rd == ex_rs1) begin
            forwardA = 2'b10;
        end else if (wb_reg_write && wb_rd != 0 && wb_rd == ex_rs1) begin
            forwardA = 2'b01;
        end
        
        // Forward B
        if (mem_reg_write && mem_rd != 0 && mem_rd == ex_rs2) begin
            forwardB = 2'b10;
        end else if (wb_reg_write && wb_rd != 0 && wb_rd == ex_rs2) begin
            forwardB = 2'b01;
        end
    end
endmodule
*/

/* Code of alu:
module alu(
    input [31:0] a,
    input [31:0] b,
    input [5:0] alu_ctrl,  // [5:4]=modo, [3:0]=operação
    output reg [31:0] result,
    output zero
);
    wire [1:0] vec_mode = alu_ctrl[5:4];
    wire [3:0] op = alu_ctrl[3:0];
    reg [7:0] b0,b1,b2,b3;
    reg [15:0] h0,h1;
    
    always @(*) begin
        case (vec_mode)
            2'b00: begin // escalar
                case (op)
                    4'b0000: result = a + b;
                    4'b0001: result = a - b;
                    4'b0010: result = a & b;
                    4'b0011: result = a | b;
                    4'b0100: result = a ^ b;
                    4'b0101: result = a << b[4:0];
                    4'b0110: result = a >> b[4:0];
                    4'b0111: result = $signed(a) >>> b[4:0];
                    4'b1000: result = b; // LUI
                    default: result = 0;
                endcase
            end
            
            2'b01: begin // 4x8 bits
                case (op)
                    4'b0000: begin // vadd.8
                        b0 = a[7:0] + b[7:0];
                        b1 = a[15:8] + b[15:8];
                        b2 = a[23:16] + b[23:16];
                        b3 = a[31:24] + b[31:24];
                        result = {b3, b2, b1, b0};
                    end
                    4'b0001: begin // vsub.8
                        b0 = a[7:0] - b[7:0];
                        b1 = a[15:8] - b[15:8];
                        b2 = a[23:16] - b[23:16];
                        b3 = a[31:24] - b[31:24];
                        result = {b3, b2, b1, b0};
                    end
                    4'b0010: result = a & b; // vand.8
                    4'b0011: result = a | b; // vor.8
                    default: result = 0;
                endcase
            end
            
            2'b10: begin // 2x16 bits
                case (op)
                    4'b0000: begin // vadd.16
                        h0 = a[15:0] + b[15:0];
                        h1 = a[31:16] + b[31:16];
                        result = {h1, h0};
                    end
                    4'b0001: begin // vsub.16
                        h0 = a[15:0] - b[15:0];
                        h1 = a[31:16] - b[31:16];
                        result = {h1, h0};
                    end
                    4'b0010: result = a & b; // vand.16
                    4'b0011: result = a | b; // vor.16
                    default: result = 0;
                endcase
            end
            
            default: result = 0;
        endcase
    end
    
    assign zero = (result == 0);
endmodule
*/

/* Code of ex_mem_reg:
module ex_mem_reg(
    input clk, 
    input reset,
    // Sinais de controle
    input reg_write_in, 
    input mem_to_reg_in, 
    input mem_read_in, 
    input mem_write_in,
    input branch_in,
    input [31:0] alu_result_in, 
    input [31:0] write_data_in, 
    input [4:0] rd_in,
    input [4:0] rs1_in,
    input [4:0] rs2_in,
    
    output reg reg_write_out, 
    output reg mem_to_reg_out, 
    output reg mem_read_out, 
    output reg mem_write_out,
    output reg branch_out,
    output reg [31:0] alu_result_out,
    output reg [31:0] write_data_out, 
    output reg [4:0] rd_out,
    output reg [4:0] rs1_out,
    output reg [4:0] rs2_out
);
    always @(posedge clk or posedge reset) begin
        if (reset) begin
            reg_write_out <= 0; mem_to_reg_out <= 0; mem_read_out <= 0;
            mem_write_out <= 0; branch_out <= 0;                     
            alu_result_out <= 0; write_data_out <= 0; 
            rd_out <= 0; rs1_out <= 0; rs2_out <= 0;                 
        end else begin
            reg_write_out <= reg_write_in; 
            mem_to_reg_out <= mem_to_reg_in;
            mem_read_out <= mem_read_in; 
            mem_write_out <= mem_write_in;
            branch_out <= branch_in;                                 
            alu_result_out <= alu_result_in; 
            write_data_out <= write_data_in;
            rd_out <= rd_in;
            rs1_out <= rs1_in; rs2_out <= rs2_in;                    
        end
    end
endmodule
*/

/* Code of hazard_unit:
module hazard_unit(
    input [4:0] id_rs1,
    input [4:0] id_rs2,
    input ex_mem_read,
    input [4:0] ex_rd,
    output reg stall
);
    always @(*) begin
        stall = 0;
        if (ex_mem_read && ex_rd != 0) begin
            if (ex_rd == id_rs1 || ex_rd == id_rs2) begin
                stall = 1;
            end
        end
    end
endmodule
*/

/* Code of mem_wb_reg:
module mem_wb_reg(
    input clk, input reset,
    input reg_write_in, input mem_to_reg_in,
    input [31:0] alu_result_in, input [31:0] mem_data_in, input [4:0] rd_in,
    output reg reg_write_out, output reg mem_to_reg_out,
    output reg [31:0] alu_result_out, output reg [31:0] mem_data_out,
    output reg [4:0] rd_out
);
    always @(posedge clk or posedge reset) begin
        if (reset) begin
            reg_write_out <= 0; mem_to_reg_out <= 0;
            alu_result_out <= 0; mem_data_out <= 0; rd_out <= 0;
        end else begin
            reg_write_out <= reg_write_in; mem_to_reg_out <= mem_to_reg_in;
            alu_result_out <= alu_result_in; mem_data_out <= mem_data_in;
            rd_out <= rd_in;
        end
    end
endmodule
*/

/* Code of pipeline_ctrl:
// pipeline_ctrl.v
module pipeline_ctrl(
    input stall,           // Do hazard_unit
    input branch_taken,    // Do estágio EX (branch foi tomado?)
    input jal_taken,       // Do estágio EX (jal foi executado?)
    input jalr_taken,      // Do estágio EX (jalr foi executado?)
    
    // Sinais de controle para o pipeline
    output reg pc_write,     // Para PC: 1=atualiza, 0=congela
    output reg if_id_write,  // Para IF/ID: 1=atualiza, 0=congela
    output reg if_id_flush,  // Para IF/ID: 1=insere NOP (flush)
    output reg id_ex_flush   // Para ID/EX: 1=insere NOP (flush)
);

    // Sinal combinado para jumps/branches
    wire jump_taken;
    assign jump_taken = branch_taken | jal_taken | jalr_taken;
    
    always @(*) begin
        // Valores padrão: tudo normal, pipeline fluindo
        pc_write = 1'b1;
        if_id_write = 1'b1;
        if_id_flush = 1'b0;
        id_ex_flush = 1'b0;
        
        // CASO 1: Stall (Load-Use Hazard)
        if (stall) begin
            // Congela o pipeline
            pc_write = 1'b0;      // PC não atualiza
            if_id_write = 1'b0;   // IF/ID não atualiza
            id_ex_flush = 1'b1;   // Insere NOP em ID/EX (bolha)
        end
        
        // CASO 2: Jump/Branch taken
        else if (jump_taken) begin
            // Descartar instruções erradas no pipeline
            if_id_flush = 1'b1;   // Descarta instrução em IF/ID
            id_ex_flush = 1'b1;   // Descarta instrução em ID/EX
        end
        
        // Se não stall nem jump, mantém valores padrão
    end
    
endmodule
*/
