// Digital circuit somador_final (1).dig as structural Verilog
module somador_final__1 (
  input  [31:0] A,
  input  [31:0] B,
  input  Mode__0__eq__SOM__1__eq__SUB,
  input  [1:0] TAM__00_eq_4__01_eq_8__10_eq_16__11_eq_32,
  output [31:0] S
);

  VEC_ADDSUB #(.applicationType("GHDL")) u_VEC_ADDSUB (
    .A_i(A), .B_i(B), .mode_i(Mode__0__eq__SOM__1__eq__SUB),
    .vecSize_i(TAM__00_eq_4__01_eq_8__10_eq_16__11_eq_32), .S_o(S));

  // Notes on the sheet:
  //   B: default 1
endmodule

/* Code of VEC_ADDSUB:
library ieee;
use ieee.std_logic_1164.all;
use ieee.numeric_std.all;

entity VEC_ADDSUB is
    port (
        A_i       : in  std_logic_vector(31 downto 0); -- input1
        B_i       : in  std_logic_vector(31 downto 0); --input2
        mode_i    : in  std_logic; --modo, 
		  --0 = soma, 
          --1= sub
        vecSize_i : in  std_logic_vector(1 downto 0); -- tamanho, 
		  --00=4b (8 operacoes simultaneas), 
		  --01=8b (4 operacoes simultaneas), 
		  --10=16b (2 operacoes simultaneas),
		  --11=32b (1 operacoes simultaneas)      
        S_o       : out std_logic_vector(31 downto 0) --output
    );
end entity;

architecture ARQ of VEC_ADDSUB is
    signal B_neg : std_logic_vector(31 downto 0); -- vetor do Not B
    
begin
    B_neg <= B_i xor (31 downto 0 => mode_i); 
    	-- se for subtracao, pegaremos o complemento de 2 do B_i: 
		--(A - B = A + (Not B))

process (A_i, B_neg, mode_i, vecSize_i)
    variable c   : std_logic;
begin
    -- Inicialização obrigatória do carry
    c := mode_i;

    for i in 0 to 31 loop

        if (i = 0) or
           (vecSize_i = "00" and i mod 4 = 0) or
           (vecSize_i = "01" and i mod 8 = 0) or
           (vecSize_i = "10" and i mod 16 = 0) or
           (vecSize_i = "11" and i = 0) then
            c := mode_i;
        end if;

        -- Soma do bit
        S_o(i) <= A_i(i) xor B_neg(i) xor c;

        c := (A_i(i) and B_neg(i)) or
             (A_i(i) and c) or
             (B_neg(i) and c);
    end loop;
end process;

end ARQ;
*/
